# Fritzing sketch Pinout (saved by Fritzing 0.9.4)
breadboards: 2

parts:
  Part1 = Arduino Mega ADK (Rev3)
  hc-sr1 = hc-sr04
  hc-sr2 = hc-sr04
  hc-sr3 = hc-sr04
  L298N1 = L298N DC motor driver
  M1 = DC Motor  # not connected
  M2 = DC Motor  # not connected
  U1 = ESP8266 NodeMCU LoLin module
  S1 = Momentary Switch [package=ksa_sealed_tac_switch]
  J1 = Piezo Speaker
  VCC1 = Battery block 9V

nets:
  N1: Part1.D19/RX1, U1.D6
  N2: Part1.D18/TX1, U1.D5
  GND: Part1.GND, hc-sr1.GND, hc-sr2.GND, hc-sr3.GND, L298N1.GND, U1.GND, S1.2, S1.4, J1.pin1, VCC1.-
  VCC: Part1.5V, hc-sr1.VCC, hc-sr2.VCC, hc-sr3.VCC
  N3: Part1.D2_PWM, L298N1.ENA
  N4: Part1.D3_PWM, L298N1.ENB
  N5: Part1.D22, hc-sr3.Echo
  N6: Part1.D23, hc-sr1.Trig, hc-sr2.Trig, hc-sr3.Trig
  N7: Part1.D24, hc-sr2.Echo
  N8: Part1.D26, hc-sr1.Echo
  N9: Part1.D44, L298N1.IN1
  N10: Part1.D45, L298N1.IN2
  N11: Part1.D46, L298N1.IN4
  N12: Part1.D47, L298N1.IN3
  N13: L298N1.12V, VCC1.+
  N14: U1.D1, J1.pin2
  N15: U1.D2, S1.1, S1.3

custom parts:
  L298N DC motor driver: 2x DC motor driver with 78M05 positive voltage regulator (7..35 V) L298N: max 46 V, 2 A Set 5 V Enable jumper to enable 5 V regultor (needed for the L298N) and +5 V output at screw terminal or supply external +5 V at screw terminal Set ENA and/or ENB to +5 V to enable motor permanently or supply ENA and/or ENB with PWM signal IN1 and IN2 set rotation directory for motor A (OUT1/OUT2) IN2 and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
  ESP8266 NodeMCU LoLin module: ESP8266 based NodeMCU
